# Fritzing sketch keyboard-ascii (saved by Fritzing 0.9.2b)
circuit board: 8.46667cm x 5.64444cm

parts:
  Part1 = Arduino Uno (Rev3)
  IC1 = IC, DIP package, 16 pins [chip_label=Keyboard]

nets:
  N1: Part1.D8, IC1.pin7
  N2: Part1.D9_PWM, IC1.pin5
  N3: Part1.D10_PWM/SS, IC1.pin6
  N4: Part1.D11_PWM/MOSI, IC1.pin11
  N5: Part1.D12/MISO, IC1.pin10
  N6: Part1.D13/SCK, IC1.pin13
  N7: Part1.D4, IC1.pin3
  N8: Part1.D5_PWM, IC1.pin2
  N9: Part1.D6_PWM, IC1.pin12
  N10: Part1.5V, IC1.pin1
  N11: Part1.GND, IC1.pin8
